# Fritzing sketch Spor_Interface_Marklin (saved by Fritzing 0.9.6b)
stripboards: 1

parts:
  R9 = Resistor [tolerance=±5% resistance=100 power=0.25 package="0805 [SMD]"]
  R10 = Resistor [tolerance=±5% resistance=100 power=0.25 package="0805 [SMD]"]
  R11 = Resistor [tolerance=±5% resistance=100 power=0.25 package="0805 [SMD]"]
  R12 = Resistor [tolerance=±5% resistance=100 power=0.25 package="0805 [SMD]"]
  R13 = Resistor [tolerance=±5% resistance=100 power=0.25 package="0805 [SMD]"]
  R14 = Resistor [tolerance=±5% resistance=100 power=0.25 package="0805 [SMD]"]
  R15 = Resistor [tolerance=±5% resistance=100 power=0.25 package="0805 [SMD]"]
  R16 = Resistor [tolerance=±5% resistance=100 power=0.25 package="0805 [SMD]"]
  U2 = PCF8574 [package="DIP16 [THT]"]
  R7 = Resistor [tolerance=±5% resistance=100 power=0.25 package="0805 [SMD]"]
  R8 = Resistor [tolerance=±5% resistance=100 power=0.25 package="0805 [SMD]"]
  R5 = Resistor [tolerance=±5% resistance=100 power=0.25 package="0805 [SMD]"]
  M1 = DOIT Esp32 DevKit v1 (30 pins long, 11 pins width) [part_number=ESP32S-PIN30]
  R3 = Resistor [tolerance=±5% resistance=100 power=0.25 package="0805 [SMD]"]
  R2 = Resistor [tolerance=±5% resistance=100 power=0.25 package="0805 [SMD]"]
  R1 = Resistor [tolerance=±5% resistance=100 power=0.25 package="0805 [SMD]"]
  R0 = Resistor [tolerance=±5% resistance=100 power=0.25 package="0805 [SMD]"]
  R6 = Resistor [tolerance=±5% resistance=100 power=0.25 package="0805 [SMD]"]
  U1 = PCF8574 [package="DIP16 [THT]"]
  J27 = male pin header, 3 pins [form="♂ (male)"]
  DFRobot_DFPlayer_Mini1 = DFRobot DFPlayer Mini [part_number=DFR0299]
  J28 = male pin header, 8 pins [form="♂ (male)"]
  J29 = male pin header, 8 pins [form="♂ (male)"]
  U18 = V_REG_LD1117VXX [package=78xxl]
  J30 = male pin header, 4 pins [form="♂ (male)"]
  J31 = male pin header, 4 pins [form="♂ (male)"]
  J32 = male pin header, 4 pins [form="♂ (male)"]
  J33 = male pin header, 4 pins [form="♂ (male)"]
  SPKR1 = Loudspeaker
  J34 = Camdenboss CTB0158-5 [part_number=CTB0158-5 package=THT]
  J35 = Camdenboss CTB0158-5 [part_number=CTB0158-5 package=THT]
  J36 = Camdenboss CTB0158-5 [part_number=CTB0158-5 package=THT]
  J37 = Camdenboss CTB0158-5 [part_number=CTB0158-5 package=THT]
  U19 = TLP620-4 [package="DIP (Dual Inline) [THT]"]
  U20 = TLP620-4 [package="DIP (Dual Inline) [THT]"]
  U21 = TLP620-4 [package="DIP (Dual Inline) [THT]"]
  U22 = TLP620-4 [package="DIP (Dual Inline) [THT]"]
  J38 = male pin header, 1 pin [form="♂ (male)"]
  J39 = male pin header, 1 pin [form="♂ (male)"]
  J40 = male pin header, 1 pin [form="♂ (male)"]
  J41 = male pin header, 1 pin [form="♂ (male)"]
  J42 = male pin header, 1 pin [form="♂ (male)"]
  J43 = male pin header, 1 pin [form="♂ (male)"]
  J44 = male pin header, 1 pin [form="♂ (male)"]
  J45 = male pin header, 1 pin [form="♂ (male)"]
  J46 = male pin header, 1 pin [form="♂ (male)"]
  J47 = male pin header, 1 pin [form="♂ (male)"]
  J48 = male pin header, 1 pin [form="♂ (male)"]
  J49 = male pin header, 1 pin [form="♂ (male)"]
  J50 = male pin header, 1 pin [form="♂ (male)"]
  J51 = male pin header, 1 pin [form="♂ (male)"]
  J52 = male pin header, 1 pin [form="♂ (male)"]
  J53 = male pin header, 1 pin [form="♂ (male)"]

nets:
  N1: R9.Pin_0, U22.pin2
  N2: R9.Pin_1, J37.pin4
  N3: R10.Pin_0, U22.pin4
  N4: R10.Pin_1, J37.pin3
  N5: R11.Pin_0, U22.pin6
  N6: R11.Pin_1, J37.pin2
  N7: R12.Pin_0, U22.pin8
  N8: R12.Pin_1, J37.pin1
  N9: R13.Pin_0, U21.pin8
  N10: R13.Pin_1, J34.pin1
  N11: R14.Pin_0, U21.pin6
  N12: R14.Pin_1, J34.pin2
  N13: R15.Pin_0, U21.pin4
  N14: R15.Pin_1, J34.pin3
  N15: R16.Pin_0, U21.pin2
  N16: R16.Pin_1, J34.pin4
  3.3V: U2.A0, U2.VCC, M1.3V3, U1.VCC, J27.pin3
  GND: U2.A1, U2.A2, U2.GND, M1.GND, U1.A0, U1.A1, U1.A2, U1.GND, J27.pin2, DFRobot_DFPlayer_Mini1.GND-1, DFRobot_DFPlayer_Mini1.GND-2, J28.pin7, J29.pin7, U18.GND, U19.pin9, U19.pin11, U19.pin13, U19.pin15, U20.pin9, U20.pin11, U20.pin13, U20.pin15, U21.pin9, U21.pin11, U21.pin13, U21.pin15, U22.pin9, U22.pin11, U22.pin13, U22.pin15
  P10: U2.P0, J33.pin1, U20.pin16, J42.pin1
  P11: U2.P1, J33.pin2, U20.pin14, J43.pin1
  P12: U2.P2, J33.pin3, U20.pin12, J44.pin1
  P13: U2.P3, J33.pin4, U20.pin10, J45.pin1
  P14: U2.P4, J32.pin4, U22.pin10, J50.pin1
  P15: U2.P5, J32.pin3, U22.pin12, J51.pin1
  P16: U2.P6, J32.pin2, U22.pin14, J52.pin1
  P17: U2.P7, J32.pin1, U22.pin16, J53.pin1
  I2C-SCL: U2.SCL, M1.D22, U1.SCL
  I2C-SDA: U2.SDA, M1.D21, U1.SDA
  N17: R7.Pin_0, U20.pin4
  N18: R7.Pin_1, J35.pin3
  N19: R8.Pin_0, U20.pin6
  N20: R8.Pin_1, J35.pin2
  N21: R5.Pin_0, U20.pin8
  N22: R5.Pin_1, J35.pin1
  cpu-tx: M1.RX2, DFRobot_DFPlayer_Mini1.RX, J28.pin2
  cpu-rx: M1.TX2, DFRobot_DFPlayer_Mini1.TX, J28.pin3
  5V: M1.VIN, J27.pin1, U18.IN
  N23: R3.Pin_0, U19.pin2
  N24: R3.Pin_1, J36.pin4
  N25: R2.Pin_0, U19.pin4
  N26: R2.Pin_1, J36.pin3
  N27: R1.Pin_0, U19.pin6
  N28: R1.Pin_1, J36.pin2
  N29: R0.Pin_0, U19.pin8
  N30: R0.Pin_1, J36.pin1
  N31: R6.Pin_0, U20.pin2
  N32: R6.Pin_1, J35.pin4
  P00: U1.P0, J31.pin1, U19.pin16, J46.pin1
  P01: U1.P1, J31.pin2, U19.pin14, J47.pin1
  P02: U1.P2, J31.pin3, U19.pin12, J48.pin1
  P03: U1.P3, J31.pin4, U19.pin10, J49.pin1
  P04: U1.P4, J30.pin4, U21.pin10, J41.pin1
  P05: U1.P5, J30.pin3, U21.pin12, J40.pin1
  P06: U1.P6, J30.pin2, U21.pin14, J39.pin1
  P07: U1.P7, J30.pin1, U21.pin16, J38.pin1
  N33: DFRobot_DFPlayer_Mini1.VCC, J28.pin1, U18.OUT
  N34: DFRobot_DFPlayer_Mini1.DAC_R, J28.pin4
  N35: DFRobot_DFPlayer_Mini1.DAC_L, J28.pin5
  N36: DFRobot_DFPlayer_Mini1.SPK_1, J28.pin6, SPKR1.pin1
  N37: DFRobot_DFPlayer_Mini1.SPK_2, J28.pin8, SPKR1.pin2
  N38: DFRobot_DFPlayer_Mini1.IO_1, J29.pin8
  N39: DFRobot_DFPlayer_Mini1.IO_2, J29.pin6
  N40: DFRobot_DFPlayer_Mini1.ADKEY_1, J29.pin5
  N41: DFRobot_DFPlayer_Mini1.ADKEY_2, J29.pin4
  N42: DFRobot_DFPlayer_Mini1.USB_POS, J29.pin3
  N43: DFRobot_DFPlayer_Mini1.USB_NEG, J29.pin2
  N44: DFRobot_DFPlayer_Mini1.BUSY, J29.pin1
  N45: J34.pin5, U21.pin1, U21.pin3, U21.pin5, U21.pin7
  N46: J35.pin5, U20.pin1, U20.pin3, U20.pin5, U20.pin7
  N47: J36.pin5, U19.pin1, U19.pin3, U19.pin5, U19.pin7
  N48: J37.pin5, U22.pin1, U22.pin3, U22.pin5, U22.pin7

notes:
  Ext. Power

custom parts:
  DOIT Esp32 DevKit v1 (30 pins long, 11 pins width): The DOIT Esp32 DevKit v1 is one of the development board created by DOIT to evaluate the ESP-WROOM-32 module. It is based on the ESP32 microcontroller that boasts Wifi, Bluetooth, Ethernet and Low Power support all in a single chip. (vanepp) made breadboard work, adjusted pin numbering and labels and reduced size of schematic and cleaned up pcb. This chip is 30pins long (2 x15) and 11 pins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
  TLP620-4: Quad Photo-transistor optically coupled to two infrared emitting diodes connected in inverse parallel.
