# Fritzing sketch ESP32_PCF8574 (saved by Fritzing 0.9.6b)
circuit board: 7.0995cm x 9.88134cm
stripboards: 1

parts:
  U2 = PCF8574 [package="DIP16 [THT]"]
  M1 = DOIT Esp32 DevKit v1 (30 pins long, 11 pins width) [part_number=ESP32S-PIN30]
  J27 = male pin header, 3 pins [form="♂ (male)"]
  J28 = female pin header, 2 pins [form="♀ (female)"]
  U1 = PCF8574 [package="DIP16 [THT]"]
  J23 = male pin header, 5 pins [form="♂ (male)"]
  J24 = male pin header, 5 pins [form="♂ (male)"]
  J25 = male pin header, 5 pins [form="♂ (male)"]
  J26 = male pin header, 5 pins [form="♂ (male)"]

nets:
  3.3V: U2.A0, U2.VCC, J27.pin3, J28.pin2, U1.VCC
  GND: U2.A1, U2.A2, U2.GND, M1.GND, J27.pin2, U1.A0, U1.A1, U1.A2, U1.GND, J23.pin5, J24.pin5, J25.pin5, J26.pin5
  N1: U2.P0, J23.pin1
  N2: U2.P1, J23.pin2
  N3: U2.P2, J23.pin3
  N4: U2.P3, J23.pin4
  N5: U2.P4, J26.pin1
  N6: U2.P5, J26.pin2
  N7: U2.P6, J26.pin3
  N8: U2.P7, J26.pin4
  INTn: U2.INT, M1.D23, U1.INT
  I2C-SCL: U2.SCL, M1.D22, U1.SCL
  I2C-SDA: U2.SDA, M1.D21, U1.SDA
  N9: M1.3V3, J28.pin1
  5V: M1.VIN, J27.pin1
  N10: U1.P0, J24.pin1
  N11: U1.P1, J24.pin2
  N12: U1.P2, J24.pin3
  N13: U1.P3, J24.pin4
  N14: U1.P4, J25.pin1
  N15: U1.P5, J25.pin2
  N16: U1.P6, J25.pin3
  N17: U1.P7, J25.pin4

notes:
  Ext. Power

custom parts:
  DOIT Esp32 DevKit v1 (30 pins long, 11 pins width): The DOIT Esp32 DevKit v1 is one of the development board created by DOIT to evaluate the ESP-WROOM-32 module. It is based on the ESP32 microcontroller that boasts Wifi, Bluetooth, Ethernet and Low Power support all in a single chip. (vanepp) made breadboard work, adjusted pin numbering and labels and reduced size of schematic and cleaned up pcb. This chip is 30pins long (2 x15) and 11 pins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
