# Fritzing sketch PCB-CPU_and_Power_2xI2C (saved by Fritzing 0.9.6b)
circuit board: 4.86295cm x 5.35847cm
stripboards: 1

parts:
  J1 = male pin header, 3 pins [form="♂ (male)"]
  J2 = male pin header, 4 pins [form="♂ (male)"]
  HW613 = female pin header, 4 pins [form="♀ (female)"]
  J4 = female pin header, 15 pins [form="♀ (female)"]
  J5 = female pin header, 15 pins [form="♀ (female)"]
  J7 = male pin header, 15 pins [form="♂ (male)"]
  J8 = male pin header, 2 pins [form="♂ (male)"]
  J10 = male pin header, 15 pins [form="♂ (male)"]
  M1 = DOIT Esp32 DevKit v1 (30 pins long, 11 pins width) [part_number=ESP32S-PIN30]  # not connected

nets:
  N1: J1.pin1, HW613.pin1
  N2: J1.pin2, HW613.pin2
  GND: J1.pin3, J2.pin4, HW613.pin3, J5.pin2, J10.pin2
  3.3V: J2.pin1, HW613.pin4, J5.pin1, J10.pin1
  I2C_SDA1: J2.pin2, J5.pin11, J8.pin1, J10.pin11
  I2C_SCL1: J2.pin3, J5.pin14, J8.pin2, J10.pin14
  N3: J4.pin1, J7.pin1
  N4: J4.pin2, J7.pin2
  N5: J4.pin3, J7.pin3
  N6: J4.pin4, J7.pin4
  N7: J4.pin5, J7.pin5
  N8: J4.pin6, J7.pin6
  N9: J4.pin7, J7.pin7
  N10: J4.pin8, J7.pin8
  N11: J4.pin9, J7.pin9
  N12: J4.pin10, J7.pin10
  N13: J4.pin11, J7.pin11
  N14: J4.pin12, J7.pin12
  N15: J4.pin13, J7.pin13
  N16: J4.pin14, J7.pin14
  N17: J4.pin15, J7.pin15
  N18: J5.pin3, J10.pin3
  N19: J5.pin4, J10.pin4
  N20: J5.pin5, J10.pin5
  N21: J5.pin6, J10.pin6
  N22: J5.pin7, J10.pin7
  N23: J5.pin8, J10.pin8
  N24: J5.pin9, J10.pin9
  N25: J5.pin10, J10.pin10
  N26: J5.pin12, J10.pin12
  N27: J5.pin13, J10.pin13
  N28: J5.pin15, J10.pin15

notes:
  Extern power
  GND
  12-24V
  SDA1
  SCL1
  SDA2
  SCL2
  3V3
  I2C Bus A
  I2C Bus B

custom parts:
  DOIT Esp32 DevKit v1 (30 pins long, 11 pins width): The DOIT Esp32 DevKit v1 is one of the development board created by DOIT to evaluate the ESP-WROOM-32 module. It is based on the ESP32 microcontroller that boasts Wifi, Bluetooth, Ethernet and Low Power support all in a single chip. (vanepp) made breadboard work, adjusted pin numbering and labels and reduced size of schematic and cleaned up pcb. This chip is 30pins long (2 x15) and 11 pins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
