# Fritzing sketch PCB-LedDriver-V3 (saved by Fritzing 0.9.6b)
circuit board: 10cm x 7.5cm
breadboards: 1

parts:
  U1 = PCF8574 [package="DIP16 [THT]"]
  U2 = PCF8574 [package="DIP16 [THT]"]
  U3 = PCF8574 [package="DIP16 [THT]"]
  U4 = PCF8574 [package="DIP16 [THT]"]
  J9 = male pin header, 4 pins [form="♂ (male)"]
  J10 = male pin header, 4 pins [form="♂ (male)"]
  J4 = male pin header, 5 pins [form="♂ (male)"]
  U5 = Sharp PC847X [package=THT]
  R13 = Resistor [tolerance=±5% power=0.25 resistance=330 package=THT]
  R14 = Resistor [tolerance=±5% power=0.25 resistance=330 package=THT]
  R15 = Resistor [tolerance=±5% power=0.25 resistance=330 package=THT]
  R16 = Resistor [tolerance=±5% power=0.25 resistance=330 package=THT]
  R32 = Resistor [tolerance=±5% power=0.25 resistance=100 package=THT]
  R34 = Resistor [tolerance=±5% power=0.25 resistance=100 package=THT]
  R33 = Resistor [tolerance=±5% power=0.25 resistance=100 package=THT]
  R35 = Resistor [tolerance=±5% power=0.25 resistance=100 package=THT]
  U6 = Sharp PC847X [package=THT]
  R49 = Resistor [tolerance=±5% power=0.25 resistance=100 package=THT]
  R50 = Resistor [tolerance=±5% power=0.25 resistance=100 package=THT]
  R51 = Resistor [tolerance=±5% power=0.25 resistance=220 package=THT]
  R52 = Resistor [tolerance=±5% power=0.25 resistance=100 package=THT]
  J14 = male pin header, 5 pins [form="♂ (male)"]
  R65 = Resistor [tolerance=±5% power=0.25 resistance=330 package=THT]
  R66 = Resistor [tolerance=±5% power=0.25 resistance=330 package=THT]
  R67 = Resistor [tolerance=±5% power=0.25 resistance=330 package=THT]
  R68 = Resistor [tolerance=±5% power=0.25 resistance=330 package=THT]
  U8 = Sharp PC847X [package=THT]
  J13 = male pin header, 5 pins [form="♂ (male)"]
  R61 = Resistor [tolerance=±5% power=0.25 resistance=330 package=THT]
  R62 = Resistor [tolerance=±5% power=0.25 resistance=330 package=THT]
  R63 = Resistor [tolerance=±5% power=0.25 resistance=330 package=THT]
  R64 = Resistor [tolerance=±5% power=0.25 resistance=330 package=THT]
  U7 = Sharp PC847X [package=THT]
  J3 = male pin header, 5 pins [form="♂ (male)"]
  R9 = Resistor [tolerance=±5% power=0.25 resistance=330 package=THT]
  R10 = Resistor [tolerance=±5% power=0.25 resistance=330 package=THT]
  R11 = Resistor [tolerance=±5% power=0.25 resistance=330 package=THT]
  R12 = Resistor [tolerance=±5% power=0.25 resistance=330 package=THT]
  R27 = Resistor [tolerance=±5% power=0.25 resistance=100 package=THT]
  R28 = Resistor [tolerance=±5% power=0.25 resistance=100 package=THT]
  R29 = Resistor [tolerance=±5% power=0.25 resistance=100 package=THT]
  R30 = Resistor [tolerance=±5% power=0.25 resistance=100 package=THT]
  R48 = Resistor [tolerance=±5% power=0.25 resistance=100 package=THT]
  R47 = Resistor [tolerance=±5% power=0.25 resistance=100 package=THT]
  R46 = Resistor [tolerance=±5% power=0.25 resistance=100 package=THT]
  R45 = Resistor [tolerance=±5% power=0.25 resistance=100 package=THT]
  R21 = Resistor [tolerance=±5% power=0.25 resistance=2.2k package=THT]
  J5 = female pin header, 2 pins [form="♀ (female)"]
  R26 = Resistor [tolerance=±5% power=0.25 resistance=2.2k package=THT]
  R31 = Resistor [tolerance=±5% power=0.25 resistance=2.2k package=THT]
  R36 = Resistor [tolerance=±5% power=0.25 resistance=2.2k package=THT]
  J6 = male pin header, 2 pins [form="♂ (male)"]
  J8 = male pin header, 2 pins [form="♂ (male)"]
  J7 = male pin header, 2 pins [form="♂ (male)"]
  U11 = Sharp PC847X [package=THT]
  U9 = Sharp PC847X [package=THT]
  J1 = male pin header, 5 pins [form="♂ (male)"]
  J2 = male pin header, 5 pins [form="♂ (male)"]
  R8 = Resistor [tolerance=±5% power=0.25 resistance=330 package=THT]
  R7 = Resistor [tolerance=±5% power=0.25 resistance=330 package=THT]
  R6 = Resistor [tolerance=±5% power=0.25 resistance=330 package=THT]
  R5 = Resistor [tolerance=±5% power=0.25 resistance=330 package=THT]
  R4 = Resistor [tolerance=±5% power=0.25 resistance=330 package=THT]
  R3 = Resistor [tolerance=±5% power=0.25 resistance=330 package=THT]
  R2 = Resistor [tolerance=±5% power=0.25 resistance=330 package=THT]
  R1 = Resistor [tolerance=±5% power=0.25 resistance=330 package=THT]
  R25 = Resistor [tolerance=±5% power=0.25 resistance=100 package=THT]
  R24 = Resistor [tolerance=±5% power=0.25 resistance=100 package=THT]
  R23 = Resistor [tolerance=±5% power=0.25 resistance=100 package=THT]
  R22 = Resistor [tolerance=±5% power=0.25 resistance=100 package=THT]
  R20 = Resistor [tolerance=±5% power=0.25 resistance=100 package=THT]
  R19 = Resistor [tolerance=±5% power=0.25 resistance=100 package=THT]
  R18 = Resistor [tolerance=±5% power=0.25 resistance=100 package=THT]
  R17 = Resistor [tolerance=±5% power=0.25 resistance=100 package=THT]
  R41 = Resistor [tolerance=±5% power=0.25 resistance=100 package=THT]
  R42 = Resistor [tolerance=±5% power=0.25 resistance=100 package=THT]
  R43 = Resistor [tolerance=±5% power=0.25 resistance=100 package=THT]
  R44 = Resistor [tolerance=±5% power=0.25 resistance=100 package=THT]
  R37 = Resistor [tolerance=±5% power=0.25 resistance=100 package=THT]
  R38 = Resistor [tolerance=±5% power=0.25 resistance=100 package=THT]
  R39 = Resistor [tolerance=±5% power=0.25 resistance=100 package=THT]
  R40 = Resistor [tolerance=±5% power=0.25 resistance=100 package=THT]
  U12 = Sharp PC847X [package=THT]
  U13 = Sharp PC847X [package=THT]
  J12 = male pin header, 5 pins [form="♂ (male)"]
  R60 = Resistor [tolerance=±5% power=0.25 resistance=330 package=THT]
  R59 = Resistor [tolerance=±5% power=0.25 resistance=330 package=THT]
  R58 = Resistor [tolerance=±5% power=0.25 resistance=330 package=THT]
  R57 = Resistor [tolerance=±5% power=0.25 resistance=330 package=THT]
  J11 = male pin header, 5 pins [form="♂ (male)"]
  R56 = Resistor [tolerance=±5% power=0.25 resistance=330 package=THT]
  R55 = Resistor [tolerance=±5% power=0.25 resistance=330 package=THT]
  R54 = Resistor [tolerance=±5% power=0.25 resistance=330 package=THT]
  R53 = Resistor [tolerance=±5% power=0.25 resistance=330 package=THT]

nets:
  GND: U1.A0, U1.A1, U1.GND, U2.A1, U2.GND, U3.A0, U3.GND, U4.GND, J9.pin4, J10.pin4, J5.pin1, J6.pin1, J8.pin1, J7.pin1
  N1: U1.A2, R36.Pin_0, J8.pin2
  L13-08: U1.P0, R35.Pin_0
  L13-06: U1.P1, R34.Pin_1
  L13-04: U1.P2, R33.Pin_0
  L13-02: U1.P3, R32.Pin_1
  N2: U1.P4, R49.Pin_0
  N3: U1.P5, R50.Pin_0
  N4: U1.P6, R51.Pin_0
  N5: U1.P7, R52.Pin_0
  I2C-SCL: U1.SCL, U2.SCL, U3.SCL, U4.SCL, J9.pin3, J10.pin3
  I2C_SDA: U1.SDA, U2.SDA, U3.SDA, U4.SDA, J9.pin2, J10.pin2
  3.3V: U1.VCC, U2.A0, U2.VCC, U3.A1, U3.VCC, U4.A0, U4.A1, U4.VCC, J9.pin1, J10.pin1, U5.Pin_1, U5.Pin_3, U5.Pin_5, U5.Pin_7, U6.Pin_1, U6.Pin_3, U6.Pin_5, U6.Pin_7, U8.Pin_1, U8.Pin_3, U8.Pin_5, U8.Pin_7, U7.Pin_1, U7.Pin_3, U7.Pin_5, U7.Pin_7, R21.Pin_1, R26.Pin_1, R31.Pin_1, R36.Pin_1, U11.Pin_1, U11.Pin_3, U11.Pin_5, U11.Pin_7, U9.Pin_1, U9.Pin_3, U9.Pin_5, U9.Pin_7, U12.Pin_1, U12.Pin_3, U12.Pin_5, U12.Pin_7, U13.Pin_1, U13.Pin_3, U13.Pin_5, U13.Pin_7
  N6: U2.A2, R31.Pin_0, J7.pin2
  N7: U2.P0, R30.Pin_0
  N8: U2.P1, R29.Pin_1
  N9: U2.P2, R28.Pin_0
  N10: U2.P3, R27.Pin_1
  N11: U2.P4, R45.Pin_0
  N12: U2.P5, R46.Pin_0
  N13: U2.P6, R47.Pin_0
  N14: U2.P7, R48.Pin_0
  N15: U3.A2, R26.Pin_0, J6.pin2
  N16: U3.P0, R25.Pin_0
  N17: U3.P1, R24.Pin_1
  N18: U3.P2, R23.Pin_0
  N19: U3.P3, R22.Pin_1
  N20: U3.P4, R41.Pin_0
  N21: U3.P5, R42.Pin_0
  N22: U3.P6, R43.Pin_0
  N23: U3.P7, R44.Pin_0
  N24: U4.A2, R21.Pin_0, J5.pin2
  N25: U4.P0, R20.Pin_0
  N26: U4.P1, R19.Pin_1
  N27: U4.P2, R18.Pin_0
  N28: U4.P3, R17.Pin_1
  N29: U4.P4, R37.Pin_0
  N30: U4.P5, R38.Pin_0
  N31: U4.P6, R39.Pin_0
  N32: U4.P7, R40.Pin_0
  N33: J4.pin1, U5.Pin_10, U5.Pin_12, U5.Pin_14, U5.Pin_16, U7.Pin_10, U7.Pin_12, U7.Pin_14, U7.Pin_16, J3.pin1, U11.Pin_10, U11.Pin_12, U11.Pin_14, U11.Pin_16, U9.Pin_10, U9.Pin_12, U9.Pin_14, U9.Pin_16, J1.pin1, J2.pin1
  N34: J4.pin2, R16.Pin_1
  N35: J4.pin3, R15.Pin_1
  N36: J4.pin4, R14.Pin_0
  N37: J4.pin5, R13.Pin_0
  N38: U5.Pin_2, R32.Pin_0
  N39: U5.Pin_4, R33.Pin_1
  N40: U5.Pin_6, R34.Pin_0
  N41: U5.Pin_8, R35.Pin_1
  N42: U5.Pin_9, R16.Pin_0
  N43: U5.Pin_11, R15.Pin_0
  N44: U5.Pin_13, R14.Pin_1
  N45: U5.Pin_15, R13.Pin_1
  N46: U6.Pin_2, R52.Pin_1
  N47: U6.Pin_4, R51.Pin_1
  N48: U6.Pin_6, R50.Pin_1
  N49: U6.Pin_8, R49.Pin_1
  N50: U6.Pin_9, R65.Pin_0
  N51: U6.Pin_10, U6.Pin_12, U6.Pin_14, U6.Pin_16, J14.pin1, U8.Pin_10, U8.Pin_12, U8.Pin_14, U8.Pin_16, J13.pin1, U12.Pin_10, U12.Pin_12, U12.Pin_14, U12.Pin_16, U13.Pin_10, U13.Pin_12, U13.Pin_14, U13.Pin_16, J12.pin1, J11.pin1
  N52: U6.Pin_11, R66.Pin_0
  N53: U6.Pin_13, R67.Pin_0
  N54: U6.Pin_15, R68.Pin_0
  N55: J14.pin2, R65.Pin_1
  N56: J14.pin3, R66.Pin_1
  N57: J14.pin4, R67.Pin_1
  N58: J14.pin5, R68.Pin_1
  N59: U8.Pin_2, R48.Pin_1
  N60: U8.Pin_4, R47.Pin_1
  N61: U8.Pin_6, R46.Pin_1
  N62: U8.Pin_8, R45.Pin_1
  N63: U8.Pin_9, R61.Pin_0
  N64: U8.Pin_11, R62.Pin_0
  N65: U8.Pin_13, R63.Pin_0
  N66: U8.Pin_15, R64.Pin_0
  N67: J13.pin2, R61.Pin_1
  N68: J13.pin3, R62.Pin_1
  N69: J13.pin4, R63.Pin_1
  N70: J13.pin5, R64.Pin_1
  N71: U7.Pin_2, R27.Pin_0
  N72: U7.Pin_4, R28.Pin_1
  N73: U7.Pin_6, R29.Pin_0
  N74: U7.Pin_8, R30.Pin_1
  N75: U7.Pin_9, R12.Pin_1
  N76: U7.Pin_11, R11.Pin_1
  N77: U7.Pin_13, R10.Pin_1
  N78: U7.Pin_15, R9.Pin_1
  N79: J3.pin2, R12.Pin_0
  N80: J3.pin3, R11.Pin_0
  N81: J3.pin4, R10.Pin_0
  N82: J3.pin5, R9.Pin_0
  N83: U11.Pin_2, R17.Pin_0
  N84: U11.Pin_4, R18.Pin_1
  N85: U11.Pin_6, R19.Pin_0
  N86: U11.Pin_8, R20.Pin_1
  N87: U11.Pin_9, R4.Pin_1
  N88: U11.Pin_11, R3.Pin_1
  N89: U11.Pin_13, R2.Pin_1
  N90: U11.Pin_15, R1.Pin_1
  N91: U9.Pin_2, R22.Pin_0
  N92: U9.Pin_4, R23.Pin_1
  N93: U9.Pin_6, R24.Pin_0
  N94: U9.Pin_8, R25.Pin_1
  N95: U9.Pin_9, R8.Pin_1
  N96: U9.Pin_11, R7.Pin_1
  N97: U9.Pin_13, R6.Pin_1
  N98: U9.Pin_15, R5.Pin_1
  N99: J1.pin2, R4.Pin_0
  N100: J1.pin3, R3.Pin_0
  N101: J1.pin4, R2.Pin_0
  N102: J1.pin5, R1.Pin_0
  N103: J2.pin2, R8.Pin_0
  N104: J2.pin3, R7.Pin_0
  N105: J2.pin4, R6.Pin_0
  N106: J2.pin5, R5.Pin_0
  N107: R41.Pin_1, U12.Pin_8
  N108: R42.Pin_1, U12.Pin_6
  N109: R43.Pin_1, U12.Pin_4
  N110: R44.Pin_1, U12.Pin_2
  N111: R37.Pin_1, U13.Pin_8
  N112: R38.Pin_1, U13.Pin_6
  N113: R39.Pin_1, U13.Pin_4
  N114: R40.Pin_1, U13.Pin_2
  N115: U12.Pin_9, R57.Pin_0
  N116: U12.Pin_11, R58.Pin_0
  N117: U12.Pin_13, R59.Pin_0
  N118: U12.Pin_15, R60.Pin_0
  N119: U13.Pin_9, R53.Pin_0
  N120: U13.Pin_11, R54.Pin_0
  N121: U13.Pin_13, R55.Pin_0
  N122: U13.Pin_15, R56.Pin_0
  N123: J12.pin2, R57.Pin_1
  N124: J12.pin3, R58.Pin_1
  N125: J12.pin4, R59.Pin_1
  N126: J12.pin5, R60.Pin_1
  N127: J11.pin2, R53.Pin_1
  N128: J11.pin3, R54.Pin_1
  N129: J11.pin4, R55.Pin_1
  N130: J11.pin5, R56.Pin_1

notes:
  3V3
  SDA
  SCL
  GND
