# Fritzing sketch PCB-LedDriver-V4.1 (saved by Fritzing 0.9.6b)
circuit board: 9.97908cm x 6.9cm
breadboards: 1

parts:
  U1 = PCF8574 [package="DIP16 [THT]"]
  U2 = PCF8574 [package="DIP16 [THT]"]
  U3 = PCF8574 [package="DIP16 [THT]"]
  U4 = PCF8574 [package="DIP16 [THT]"]
  J9 = male pin header, 4 pins [form="♂ (male)"]
  J10 = male pin header, 4 pins [form="♂ (male)"]
  U5 = Sharp PC847X [package=THT]
  R14 = Resistor [tolerance=±5% power=0.25 resistance=330 package=THT]
  R16 = Resistor [tolerance=±5% power=0.25 resistance=330 package=THT]
  R32 = Resistor [tolerance=±5% power=0.25 resistance=100 package=THT]
  R34 = Resistor [tolerance=±5% power=0.25 resistance=100 package=THT]
  R33 = Resistor [tolerance=±5% power=0.25 resistance=100 package=THT]
  R35 = Resistor [tolerance=±5% power=0.25 resistance=100 package=THT]
  U6 = Sharp PC847X [package=THT]
  R49 = Resistor [tolerance=±5% power=0.25 resistance=100 package=THT]
  R50 = Resistor [tolerance=±5% power=0.25 resistance=100 package=THT]
  R51 = Resistor [tolerance=±5% power=0.25 resistance=100 package=THT]
  R52 = Resistor [tolerance=±5% power=0.25 resistance=100 package=THT]
  R65 = Resistor [tolerance=±5% power=0.25 resistance=330 package=THT]
  R66 = Resistor [tolerance=±5% power=0.25 resistance=330 package=THT]
  R67 = Resistor [tolerance=±5% power=0.25 resistance=330 package=THT]
  R68 = Resistor [tolerance=±5% power=0.25 resistance=330 package=THT]
  U8 = Sharp PC847X [package=THT]
  R61 = Resistor [tolerance=±5% power=0.25 resistance=330 package=THT]
  R62 = Resistor [tolerance=±5% power=0.25 resistance=330 package=THT]
  R63 = Resistor [tolerance=±5% power=0.25 resistance=330 package=THT]
  R64 = Resistor [tolerance=±5% power=0.25 resistance=330 package=THT]
  U7 = Sharp PC847X [package=THT]
  R9 = Resistor [tolerance=±5% power=0.25 resistance=330 package=THT]
  R10 = Resistor [tolerance=±5% power=0.25 resistance=330 package=THT]
  R11 = Resistor [tolerance=±5% power=0.25 resistance=330 package=THT]
  R12 = Resistor [tolerance=±5% power=0.25 resistance=330 package=THT]
  R27 = Resistor [tolerance=±5% power=0.25 resistance=100 package=THT]
  R28 = Resistor [tolerance=±5% power=0.25 resistance=100 package=THT]
  R29 = Resistor [tolerance=±5% power=0.25 resistance=100 package=THT]
  R30 = Resistor [tolerance=±5% power=0.25 resistance=100 package=THT]
  R48 = Resistor [tolerance=±5% power=0.25 resistance=100 package=THT]
  R47 = Resistor [tolerance=±5% power=0.25 resistance=100 package=THT]
  R46 = Resistor [tolerance=±5% power=0.25 resistance=100 package=THT]
  R45 = Resistor [tolerance=±5% power=0.25 resistance=100 package=THT]
  U11 = Sharp PC847X [package=THT]
  U9 = Sharp PC847X [package=THT]
  R8 = Resistor [tolerance=±5% power=0.25 resistance=330 package=THT]
  R7 = Resistor [tolerance=±5% power=0.25 resistance=330 package=THT]
  R6 = Resistor [tolerance=±5% power=0.25 resistance=330 package=THT]
  R5 = Resistor [tolerance=±5% power=0.25 resistance=330 package=THT]
  R25 = Resistor [tolerance=±5% power=0.25 resistance=100 package=THT]
  R24 = Resistor [tolerance=±5% power=0.25 resistance=100 package=THT]
  R23 = Resistor [tolerance=±5% power=0.25 resistance=100 package=THT]
  R22 = Resistor [tolerance=±5% power=0.25 resistance=100 package=THT]
  R20 = Resistor [tolerance=±5% power=0.25 resistance=100 package=THT]
  R19 = Resistor [tolerance=±5% power=0.25 resistance=100 package=THT]
  R17 = Resistor [tolerance=±5% power=0.25 resistance=100 package=THT]
  R41 = Resistor [tolerance=±5% power=0.25 resistance=100 package=THT]
  R42 = Resistor [tolerance=±5% power=0.25 resistance=100 package=THT]
  R43 = Resistor [tolerance=±5% power=0.25 resistance=100 package=THT]
  R44 = Resistor [tolerance=±5% power=0.25 resistance=100 package=THT]
  R37 = Resistor [tolerance=±5% power=0.25 resistance=100 package=THT]
  R38 = Resistor [tolerance=±5% power=0.25 resistance=100 package=THT]
  R39 = Resistor [tolerance=±5% power=0.25 resistance=100 package=THT]
  R40 = Resistor [tolerance=±5% power=0.25 resistance=100 package=THT]
  U12 = Sharp PC847X [package=THT]
  U13 = Sharp PC847X [package=THT]
  R60 = Resistor [tolerance=±5% power=0.25 resistance=330 package=THT]
  R59 = Resistor [tolerance=±5% power=0.25 resistance=330 package=THT]
  R58 = Resistor [tolerance=±5% power=0.25 resistance=330 package=THT]
  R57 = Resistor [tolerance=±5% power=0.25 resistance=330 package=THT]
  R56 = Resistor [tolerance=±5% power=0.25 resistance=330 package=THT]
  R55 = Resistor [tolerance=±5% power=0.25 resistance=330 package=THT]
  R54 = Resistor [tolerance=±5% power=0.25 resistance=330 package=THT]
  R53 = Resistor [tolerance=±5% power=0.25 resistance=330 package=THT]
  J4 = male pin header, 8 pins [form="♂ (male)"]
  J2 = male pin header, 8 pins [form="♂ (male)"]
  J1 = male pin header, 8 pins [form="♂ (male)"]
  R4 = Resistor [tolerance=±5% power=0.25 resistance=330 package=THT]
  R3 = Resistor [tolerance=±5% power=0.25 resistance=330 package=THT]
  R1 = Resistor [tolerance=±5% power=0.25 resistance=330 package=THT]
  R2 = Resistor [tolerance=±5% power=0.25 resistance=330 package=THT]
  J11 = male pin header, 8 pins [form="♂ (male)"]
  J12 = male pin header, 8 pins [form="♂ (male)"]
  J13 = male pin header, 8 pins [form="♂ (male)"]
  J14 = male pin header, 8 pins [form="♂ (male)"]
  Pad1 = Pad [width=2 height=1 connect=center]
  Pad2 = Pad [width=2 height=1 connect=center]
  Pad3 = Pad [width=2 height=1 connect=center]
  Pad4 = Pad [width=2 height=1 connect=center]
  Pad5 = Pad [width=2 height=1 connect=center]
  Pad6 = Pad [width=2 height=1 connect=center]
  Pad7 = Pad [width=2 height=1 connect=center]
  Pad8 = Pad [width=2 height=1 connect=center]
  Pad9 = Pad [width=2 height=1 connect=center]
  Pad10 = Pad [width=2 height=1 connect=center]
  Pad11 = Pad [width=2 height=1 connect=center]
  Pad12 = Pad [width=2 height=1 connect=center]
  Pad13 = Pad [width=2 height=1 connect=center]
  Pad14 = Pad [width=2 height=1 connect=center]
  Pad15 = Pad [width=2 height=1 connect=center]
  Pad16 = Pad [width=2 height=1 connect=center]
  Pad17 = Pad [width=2 height=1 connect=center]
  Pad18 = Pad [width=2 height=1 connect=center]
  Pad19 = Pad [width=2 height=1 connect=center]
  Pad20 = Pad [width=2 height=1 connect=center]
  Pad21 = Pad [width=2 height=1 connect=center]
  Pad22 = Pad [width=2 height=1 connect=center]
  Pad23 = Pad [width=2 height=1 connect=center]
  Pad24 = Pad [width=2 height=1 connect=center]
  Pad25 = Pad [width=2 height=1 connect=center]
  Pad26 = Pad [width=2 height=1 connect=center]
  Pad27 = Pad [width=2 height=1 connect=center]
  Pad28 = Pad [width=2 height=1 connect=center]
  Pad29 = Pad [width=2 height=1 connect=center]
  Pad30 = Pad [width=2 height=1 connect=center]
  Pad31 = Pad [width=2 height=1 connect=center]
  Pad32 = Pad [width=2 height=1 connect=center]
  Pad33 = Pad [width=2 height=1 connect=center]
  Pad34 = Pad [width=2 height=1 connect=center]
  Pad35 = Pad [width=2 height=1 connect=center]
  Pad36 = Pad [width=2 height=1 connect=center]
  Pad37 = Pad [width=2 height=1 connect=center]
  Pad38 = Pad [width=2 height=1 connect=center]
  Pad39 = Pad [width=2 height=1 connect=center]
  Pad40 = Pad [width=2 height=1 connect=center]
  Pad41 = Pad [width=2 height=1 connect=center]
  Pad42 = Pad [width=2 height=1 connect=center]
  Pad43 = Pad [width=2 height=1 connect=center]
  Pad44 = Pad [width=2 height=1 connect=center]
  Pad45 = Pad [width=2 height=1 connect=center]
  Pad46 = Pad [width=2 height=1 connect=center]
  Pad47 = Pad [width=2 height=1 connect=center]
  Pad48 = Pad [width=2 height=1 connect=center]
  Pad49 = Pad [width=2 height=1 connect=center]
  Pad50 = Pad [width=2 height=1 connect=center]
  Pad51 = Pad [width=2 height=1 connect=center]
  Pad52 = Pad [width=2 height=1 connect=center]
  Pad53 = Pad [width=2 height=1 connect=center]
  Pad54 = Pad [width=2 height=1 connect=center]
  Pad55 = Pad [width=2 height=1 connect=center]
  Pad56 = Pad [width=2 height=1 connect=center]
  Pad57 = Pad [width=2 height=1 connect=center]
  Pad58 = Pad [width=2 height=1 connect=center]
  Pad59 = Pad [width=2 height=1 connect=center]
  Pad60 = Pad [width=2 height=1 connect=center]
  Pad61 = Pad [width=2 height=1 connect=center]
  Pad62 = Pad [width=2 height=1 connect=center]
  Pad63 = Pad [width=2 height=1 connect=center]
  Pad64 = Pad [width=2 height=1 connect=center]
  Pad65 = Pad [width=1 height=2 connect=center]
  Pad66 = Pad [width=1 height=2 connect=center]
  Pad67 = Pad [width=1 height=2 connect=center]
  Pad68 = Pad [width=1 height=2 connect=center]
  Pad69 = Pad [width=1 height=2 connect=center]
  Pad70 = Pad [width=1 height=2 connect=center]
  Pad71 = Pad [width=1 height=2 connect=center]
  Pad72 = Pad [width=1 height=2 connect=center]
  Pad73 = Pad [width=1 height=2 connect=center]
  Pad74 = Pad [width=1 height=2 connect=center]
  Pad75 = Pad [width=1 height=2 connect=center]
  Pad76 = Pad [width=1 height=2 connect=center]
  J3 = male pin header, 8 pins [form="♂ (male)"]
  R13 = Resistor [tolerance=±5% power=0.25 resistance=330 package=THT]
  R15 = Resistor [tolerance=±5% power=0.25 resistance=330 package=THT]
  R18 = Resistor [tolerance=±5% power=0.25 resistance=100 package=THT]

nets:
  GND: U1.A0, U1.A1, U1.A2, U1.GND, U2.A1, U2.A2, U2.GND, U3.A0, U3.A2, U3.GND, U4.A2, U4.GND, J9.pin4, J10.pin4, Pad65.pad, Pad66.pad, Pad68.pad, Pad70.pad, Pad72.pad, Pad73.pad, Pad74.pad, Pad76.pad
  L01-04: U1.P0, R35.Pin_0
  L01-05: U1.P1, R34.Pin_1
  L01-06: U1.P2, R33.Pin_0
  L01-07: U1.P3, R32.Pin_1
  L01-09: U1.P4, R49.Pin_0
  L01-10: U1.P5, R50.Pin_0
  L01-11: U1.P6, R51.Pin_0
  L01-12: U1.P7, R52.Pin_0
  INT: U1.INT, U2.INT, U3.INT, U4.INT
  I2C-SCL: U1.SCL, U2.SCL, U3.SCL, U4.SCL, J9.pin3, J10.pin3
  I2C_SDA: U1.SDA, U2.SDA, U3.SDA, U4.SDA, J9.pin2, J10.pin2
  3.3V: U1.VCC, U2.A0, U2.VCC, U3.A1, U3.VCC, U4.A0, U4.A1, U4.VCC, J9.pin1, J10.pin1, U5.Pin_1, U5.Pin_3, U5.Pin_5, U5.Pin_7, U6.Pin_1, U6.Pin_3, U6.Pin_5, U6.Pin_7, U8.Pin_1, U8.Pin_3, U8.Pin_5, U8.Pin_7, U7.Pin_1, U7.Pin_3, U7.Pin_5, U7.Pin_7, U11.Pin_1, U11.Pin_3, U11.Pin_5, U11.Pin_7, U9.Pin_1, U9.Pin_3, U9.Pin_5, U9.Pin_7, U12.Pin_1, U12.Pin_3, U12.Pin_5, U12.Pin_7, U13.Pin_1, U13.Pin_3, U13.Pin_5, U13.Pin_7, Pad67.pad, Pad69.pad, Pad71.pad, Pad75.pad
  L02-04: U2.P0, R30.Pin_0
  L02-05: U2.P1, R29.Pin_1
  L02-06: U2.P2, R28.Pin_0
  L02-07: U2.P3, R27.Pin_1
  L02-09: U2.P4, R45.Pin_0
  L02-10: U2.P5, R46.Pin_0
  L02-11: U2.P6, R47.Pin_0
  L02-12: U2.P7, R48.Pin_0
  L03-04: U3.P0, R25.Pin_0
  L03-05: U3.P1, R24.Pin_1
  L03-06: U3.P2, R23.Pin_0
  L03-07: U3.P3, R22.Pin_1
  L03-09: U3.P4, R41.Pin_0
  L03-10: U3.P5, R42.Pin_0
  L03-11: U3.P6, R43.Pin_0
  L03-12: U3.P7, R44.Pin_0
  L04-04: U4.P0, R20.Pin_0
  L04-05: U4.P1, R19.Pin_1
  L04-06: U4.P2, R18.Pin_0
  L04-07: U4.P3, R17.Pin_1
  L04-09: U4.P4, R37.Pin_0
  L04-10: U4.P5, R38.Pin_0
  L04-11: U4.P6, R39.Pin_0
  L04-12: U4.P7, R40.Pin_0
  N1: U5.Pin_2, R32.Pin_0
  N2: U5.Pin_4, R33.Pin_1
  N3: U5.Pin_6, R34.Pin_0
  N4: U5.Pin_8, R35.Pin_1
  N5: U5.Pin_9, R16.Pin_0
  N6: U5.Pin_10, U5.Pin_12, U5.Pin_14, U5.Pin_16, U7.Pin_10, U7.Pin_12, U7.Pin_14, U7.Pin_16, U11.Pin_10, U11.Pin_12, U11.Pin_14, U11.Pin_16, U9.Pin_10, U9.Pin_12, U9.Pin_14, U9.Pin_16, J4.pin2, J4.pin4, J4.pin6, J4.pin8, J2.pin2, J2.pin4, J2.pin6, J2.pin8, J1.pin2, J1.pin4, J1.pin6, J1.pin8, Pad1.pad, Pad2.pad, Pad3.pad, Pad4.pad, Pad5.pad, Pad6.pad, Pad7.pad, Pad8.pad, Pad9.pad, Pad10.pad, Pad11.pad, Pad12.pad, Pad13.pad, Pad14.pad, Pad15.pad, Pad16.pad, Pad17.pad, Pad18.pad, Pad19.pad, Pad20.pad, Pad21.pad, Pad22.pad, Pad23.pad, Pad24.pad, Pad25.pad, Pad26.pad, Pad27.pad, Pad28.pad, Pad29.pad, Pad30.pad, Pad31.pad, Pad32.pad, J3.pin2, J3.pin4, J3.pin6, J3.pin8
  N7: U5.Pin_11, R15.Pin_0
  N8: U5.Pin_13, R14.Pin_0, R14.Pin_1, J4.pin5
  N9: U5.Pin_15, R13.Pin_1
  N10: R16.Pin_1, J4.pin1
  N11: U6.Pin_2, R52.Pin_1
  N12: U6.Pin_4, R51.Pin_1
  N13: U6.Pin_6, R50.Pin_1
  N14: U6.Pin_8, R49.Pin_1
  N15: U6.Pin_9, R65.Pin_0
  N16: U6.Pin_10, U6.Pin_12, U6.Pin_14, U6.Pin_16, U8.Pin_10, U8.Pin_12, U8.Pin_14, U8.Pin_16, U12.Pin_10, U12.Pin_12, U12.Pin_14, U12.Pin_16, U13.Pin_10, U13.Pin_12, U13.Pin_14, U13.Pin_16, J11.pin2, J11.pin4, J11.pin6, J11.pin8, J12.pin2, J12.pin4, J12.pin6, J12.pin8, J13.pin2, J13.pin4, J13.pin6, J13.pin8, J14.pin2, J14.pin4, J14.pin6, J14.pin8, Pad33.pad, Pad34.pad, Pad35.pad, Pad36.pad, Pad37.pad, Pad38.pad, Pad39.pad, Pad40.pad, Pad41.pad, Pad42.pad, Pad43.pad, Pad44.pad, Pad45.pad, Pad46.pad, Pad47.pad, Pad48.pad, Pad49.pad, Pad50.pad, Pad51.pad, Pad52.pad, Pad53.pad, Pad54.pad, Pad55.pad, Pad56.pad, Pad57.pad, Pad58.pad, Pad59.pad, Pad60.pad, Pad61.pad, Pad62.pad, Pad63.pad, Pad64.pad
  N17: U6.Pin_11, R66.Pin_0
  N18: U6.Pin_13, R67.Pin_0
  N19: U6.Pin_15, R68.Pin_0
  N20: R65.Pin_1, J14.pin1
  N21: R66.Pin_1, J14.pin3
  N22: R67.Pin_1, J14.pin5
  N23: R68.Pin_1, J14.pin7
  N24: U8.Pin_2, R48.Pin_1
  N25: U8.Pin_4, R47.Pin_1
  N26: U8.Pin_6, R46.Pin_1
  N27: U8.Pin_8, R45.Pin_1
  N28: U8.Pin_9, R61.Pin_0
  N29: U8.Pin_11, R62.Pin_0
  N30: U8.Pin_13, R63.Pin_0
  N31: U8.Pin_15, R64.Pin_0
  N32: R61.Pin_1, J13.pin1
  N33: R62.Pin_1, J13.pin3
  N34: R63.Pin_1, J13.pin5
  N35: R64.Pin_1, J13.pin7
  N36: U7.Pin_2, R27.Pin_0
  N37: U7.Pin_4, R28.Pin_1
  N38: U7.Pin_6, R29.Pin_0
  N39: U7.Pin_8, R30.Pin_1
  N40: U7.Pin_9, R12.Pin_1
  N41: U7.Pin_11, R11.Pin_1
  N42: U7.Pin_13, R10.Pin_1
  N43: U7.Pin_15, R9.Pin_1
  N44: R9.Pin_0, J3.pin7
  N45: R10.Pin_0, J3.pin5
  N46: R11.Pin_0, J3.pin3
  N47: R12.Pin_0, J3.pin1
  N48: U11.Pin_2, R17.Pin_0
  N49: U11.Pin_4, R18.Pin_1
  N50: U11.Pin_6, R19.Pin_0
  N51: U11.Pin_8, R20.Pin_1
  N52: U11.Pin_9, R4.Pin_1
  N53: U11.Pin_11, R3.Pin_1
  N54: U11.Pin_13, R2.Pin_1
  N55: U11.Pin_15, R1.Pin_1
  N56: U9.Pin_2, R22.Pin_0
  N57: U9.Pin_4, R23.Pin_1
  N58: U9.Pin_6, R24.Pin_0
  N59: U9.Pin_8, R25.Pin_1
  N60: U9.Pin_9, R8.Pin_1
  N61: U9.Pin_11, R7.Pin_1
  N62: U9.Pin_13, R6.Pin_1
  N63: U9.Pin_15, R5.Pin_1
  N64: R8.Pin_0, J2.pin1
  N65: R7.Pin_0, J2.pin3
  N66: R6.Pin_0, J2.pin5
  N67: R5.Pin_0, J2.pin7
  N68: R41.Pin_1, U12.Pin_8
  N69: R42.Pin_1, U12.Pin_6
  N70: R43.Pin_1, U12.Pin_4
  N71: R44.Pin_1, U12.Pin_2
  N72: R37.Pin_1, U13.Pin_8
  N73: R38.Pin_1, U13.Pin_6
  N74: R39.Pin_1, U13.Pin_4
  N75: R40.Pin_1, U13.Pin_2
  N76: U12.Pin_9, R57.Pin_0
  N77: U12.Pin_11, R58.Pin_0
  N78: U12.Pin_13, R59.Pin_0
  N79: U12.Pin_15, R60.Pin_0
  N80: U13.Pin_9, R53.Pin_0
  N81: U13.Pin_11, R54.Pin_0
  N82: U13.Pin_13, R55.Pin_0
  N83: U13.Pin_15, R56.Pin_0
  N84: R60.Pin_1, J12.pin7
  N85: R59.Pin_1, J12.pin5
  N86: R58.Pin_1, J12.pin3
  N87: R57.Pin_1, J12.pin1
  N88: R56.Pin_1, J11.pin7
  N89: R55.Pin_1, J11.pin5
  N90: R54.Pin_1, J11.pin3
  N91: R53.Pin_1, J11.pin1
  N92: J4.pin3, R15.Pin_1
  N93: J4.pin7, R13.Pin_0
  N94: J1.pin1, R4.Pin_0
  N95: J1.pin3, R3.Pin_0
  N96: J1.pin5, R2.Pin_0
  N97: J1.pin7, R1.Pin_0

notes:
  3V3
  SDA
  SCL
  GND
  Svenn-Erik K. Thomsen
  sekt1953@gmail.com
  Track-LedDriver
  Track-LedDriver v4.0
  https://github.com/sekt1953/Modeltog-med-Home-Assistant
