# Fritzing sketch TrackInterface (saved by Fritzing 0.9.6b)

parts:
  D1 = Rectifier Diode [part_number=1N5400 package="300 mil [THT]"]
  D2 = Rectifier Diode [part_number=1N5400 package="300 mil [THT]"]
  D3 = Rectifier Diode [part_number=1N5400 package="300 mil [THT]"]
  D4 = Rectifier Diode [part_number=1N5400 package="300 mil [THT]"]
  D5 = Rectifier Diode [part_number=1N5400 package="300 mil [THT]"]
  D6 = Rectifier Diode [part_number=1N5400 package="300 mil [THT]"]
  D7 = Rectifier Diode [part_number=1N5400 package="300 mil [THT]"]
  D8 = Rectifier Diode [part_number=1N5400 package="300 mil [THT]"]
  D9 = Rectifier Diode [part_number=1N5400 package="300 mil [THT]"]
  D10 = Rectifier Diode [part_number=1N5400 package="300 mil [THT]"]
  D11 = Rectifier Diode [part_number=1N5400 package="300 mil [THT]"]
  D12 = Rectifier Diode [part_number=1N5400 package="300 mil [THT]"]
  D13 = Rectifier Diode [part_number=1N5400 package="300 mil [THT]"]
  D14 = Rectifier Diode [part_number=1N5400 package="300 mil [THT]"]
  D15 = Rectifier Diode [part_number=1N5400 package="300 mil [THT]"]
  D16 = Rectifier Diode [part_number=1N5400 package="300 mil [THT]"]
  D17 = Rectifier Diode [part_number=1N5400 package="300 mil [THT]"]
  D18 = Rectifier Diode [part_number=1N5400 package="300 mil [THT]"]
  D19 = Rectifier Diode [part_number=1N5400 package="300 mil [THT]"]
  D20 = Rectifier Diode [part_number=1N5400 package="300 mil [THT]"]
  D21 = Rectifier Diode [part_number=1N5400 package="300 mil [THT]"]
  D22 = Rectifier Diode [part_number=1N5400 package="300 mil [THT]"]
  D23 = Rectifier Diode [part_number=1N5400 package="300 mil [THT]"]
  D24 = Rectifier Diode [part_number=1N5400 package="300 mil [THT]"]
  D25 = Rectifier Diode [part_number=1N5400 package="300 mil [THT]"]
  D26 = Rectifier Diode [part_number=1N5400 package="300 mil [THT]"]
  D27 = Rectifier Diode [part_number=1N5400 package="300 mil [THT]"]
  D28 = Rectifier Diode [part_number=1N5400 package="300 mil [THT]"]
  D29 = Rectifier Diode [part_number=1N5400 package="300 mil [THT]"]
  D30 = Rectifier Diode [part_number=1N5400 package="300 mil [THT]"]
  D31 = Rectifier Diode [part_number=1N5400 package="300 mil [THT]"]
  D32 = Rectifier Diode [part_number=1N5400 package="300 mil [THT]"]
  D33 = Rectifier Diode [part_number=1N5400 package="300 mil [THT]"]
  D34 = Rectifier Diode [part_number=1N5400 package="300 mil [THT]"]
  D35 = Rectifier Diode [part_number=1N5400 package="300 mil [THT]"]
  D36 = Rectifier Diode [part_number=1N5400 package="300 mil [THT]"]
  J1 = male pin header, 18 pins [form="♂ (male)"]
  D37 = Rectifier Diode [part_number=1N5400 package="300 mil [THT]"]
  D38 = Rectifier Diode [part_number=1N5400 package="300 mil [THT]"]
  D39 = Rectifier Diode [part_number=1N5400 package="300 mil [THT]"]
  D40 = Rectifier Diode [part_number=1N5400 package="300 mil [THT]"]
  D41 = Rectifier Diode [part_number=1N5400 package="300 mil [THT]"]
  D42 = Rectifier Diode [part_number=1N5400 package="300 mil [THT]"]
  D43 = Rectifier Diode [part_number=1N5400 package="300 mil [THT]"]
  D44 = Rectifier Diode [part_number=1N5400 package="300 mil [THT]"]
  D45 = Rectifier Diode [part_number=1N5400 package="300 mil [THT]"]
  D46 = Rectifier Diode [part_number=1N5400 package="300 mil [THT]"]
  D47 = Rectifier Diode [part_number=1N5400 package="300 mil [THT]"]
  D48 = Rectifier Diode [part_number=1N5400 package="300 mil [THT]"]

nets:
  N1: D1.cathode, D2.anode
  Track Power/TrackSensor Line: D1.anode, D4.cathode, D11.cathode, D12.anode, D15.cathode, D18.anode, D21.cathode, D24.anode, D26.anode, D28.cathode, D32.cathode, D36.anode, J1.pin1, J1.pin2, D38.anode, D41.cathode, D44.anode, D47.cathode
  N2: D2.cathode, D3.anode
  Track_00/Tracksensor_00: D3.cathode, D6.anode, J1.pin3, J1.pin4
  N3: D4.anode, D5.cathode
  N4: D5.anode, D6.cathode
  Track_01/Tracksensor_01: D7.cathode, D9.anode, J1.pin5, J1.pin6
  N5: D7.anode, D8.cathode
  N6: D8.anode, D12.cathode
  N7: D9.cathode, D10.anode
  N8: D10.cathode, D11.anode
  Track_02/Tracksensor_02: D13.cathode, D16.anode, J1.pin7, J1.pin8
  N9: D13.anode, D14.cathode
  N10: D14.anode, D18.cathode
  N11: D15.anode, D17.cathode
  N12: D16.cathode, D17.anode
  Track_03/Tracksensor_03: D19.cathode, D22.anode, J1.pin9, J1.pin10
  N13: D19.anode, D20.cathode
  N14: D20.anode, D24.cathode
  N15: D21.anode, D23.cathode
  N16: D22.cathode, D23.anode
  N17: D25.cathode, D32.anode
  N18: D25.anode, D34.cathode
  N19: D26.cathode, D35.anode
  N20: D27.cathode, D31.anode
  Track_05/Tracksensor_05: D27.anode, D33.cathode, J1.pin13, J1.pin14
  N21: D28.anode, D31.cathode
  Track_04/Tracksensor_04: D29.cathode, D34.anode, J1.pin11, J1.pin12
  N22: D29.anode, D30.cathode
  N23: D30.anode, D36.cathode
  N24: D33.anode, D35.cathode
  Track_06/Tracksensor_06: J1.pin15, J1.pin16, D39.anode, D40.cathode
  Track_07/Tracksensor_07: J1.pin17, J1.pin18, D45.cathode, D48.anode
  N25: D37.cathode, D45.anode
  N26: D37.anode, D38.cathode
  N27: D39.cathode, D46.anode
  N28: D40.anode, D42.cathode
  N29: D41.anode, D43.cathode
  N30: D42.anode, D44.cathode
  N31: D43.anode, D48.cathode
  N32: D46.cathode, D47.anode
