# Fritzing sketch pcb_001 (saved by Fritzing 0.9.6b)
circuit board: 10cm x 7.5cm
breadboards: 1

parts:
  U100 = PCF8574 [package="DIP16 [THT]"]
  J4 = double row male pin header, 6 pins [form="♂ (male)"]
  U108 = TLP620-4 [package="DIP (Dual Inline) [THT]"]
  2k2_Sil1 = female pin header, 8 pins [form="♀ (female)"]
  U104 = TLP620-4 [package="DIP (Dual Inline) [THT]"]
  J5 = male pin header, 4 pins [form="♂ (male)"]
  U105 = TLP620-4 [package="DIP (Dual Inline) [THT]"]
  U101 = PCF8574 [package="DIP16 [THT]"]
  U109 = TLP620-4 [package="DIP (Dual Inline) [THT]"]
  J9 = double row male pin header, 6 pins [form="♂ (male)"]
  2k2_Sil3 = female pin header, 8 pins [form="♀ (female)"]
  2k2_Sil4 = female pin header, 5 pins [form="♀ (female)"]
  2k2_Sil5 = female pin header, 5 pins [form="♀ (female)"]
  U106 = TLP620-4 [package="DIP (Dual Inline) [THT]"]
  U107 = TLP620-4 [package="DIP (Dual Inline) [THT]"]
  U102 = PCF8574 [package="DIP16 [THT]"]
  U103 = PCF8574 [package="DIP16 [THT]"]
  2k2_Sil6 = female pin header, 8 pins [form="♀ (female)"]
  2k2_Sil7 = female pin header, 8 pins [form="♀ (female)"]
  J10 = double row male pin header, 6 pins [form="♂ (male)"]
  J11 = double row male pin header, 6 pins [form="♂ (male)"]
  2k2_Sil8 = female pin header, 5 pins [form="♀ (female)"]
  2k2_Sil9 = female pin header, 5 pins [form="♀ (female)"]
  U111 = TLP620-4 [package="DIP (Dual Inline) [THT]"]
  J8 = male pin header, 5 pins [form="♂ (male)"]
  J12 = male pin header, 5 pins [form="♂ (male)"]
  J13 = male pin header, 5 pins [form="♂ (male)"]
  J6 = male pin header, 5 pins [form="♂ (male)" part_number=5556.05A]
  J7-4x470ohm = female pin header, 5 pins [form="♀ (female)" part_number=10F5347]
  R21 = Resistor [tolerance=±5% power=0.25 resistance=22 package=THT]
  R22 = Resistor [tolerance=±5% power=0.25 resistance=22 package=THT]
  R23 = Resistor [tolerance=±5% power=0.25 resistance=22 package=THT]
  R24 = Resistor [tolerance=±5% power=0.25 resistance=22 package=THT]
  J14-4x470ohm = female pin header, 5 pins [form="♀ (female)"]
  J15 = female pin header, 5 pins [form="♀ (female)"]
  J16 = female pin header, 5 pins [form="♀ (female)"]
  R25 = Resistor [tolerance=±5% power=0.25 resistance=22 package=THT]
  R26 = Resistor [tolerance=±5% power=0.25 resistance=22 package=THT]
  R27 = Resistor [tolerance=±5% power=0.25 resistance=22 package=THT]
  R28 = Resistor [tolerance=±5% power=0.25 resistance=22 package=THT]
  R29 = Resistor [tolerance=±5% power=0.25 resistance=22 package=THT]
  R30 = Resistor [tolerance=±5% power=0.25 resistance=22 package=THT]
  R31 = Resistor [tolerance=±5% power=0.25 resistance=22 package=THT]
  R32 = Resistor [tolerance=±5% power=0.25 resistance=22 package=THT]
  R33 = Resistor [tolerance=±5% power=0.25 resistance=22 package=THT]
  R34 = Resistor [tolerance=±5% power=0.25 resistance=220 package=THT]
  R35 = Resistor [tolerance=±5% power=0.25 resistance=22 package=THT]
  R36 = Resistor [tolerance=±5% power=0.25 resistance=22 package=THT]
  J18 = male pin header, 5 pins [form="♂ (male)"]
  J19 = male pin header, 5 pins [form="♂ (male)"]
  J20 = male pin header, 5 pins [form="♂ (male)"]
  J21 = male pin header, 5 pins [form="♂ (male)"]
  J22 = female pin header, 5 pins [form="♀ (female)"]
  J23 = female pin header, 5 pins [form="♀ (female)"]
  J24 = female pin header, 5 pins [form="♀ (female)"]
  J25 = female pin header, 5 pins [form="♀ (female)"]
  R37 = Resistor [tolerance=±5% power=0.25 resistance=220 package=THT]
  R38 = Resistor [tolerance=±5% power=0.25 resistance=220 package=THT]
  R39 = Resistor [tolerance=±5% power=0.25 resistance=220 package=THT]
  R40 = Resistor [tolerance=±5% power=0.25 resistance=220 package=THT]
  R41 = Resistor [tolerance=±5% power=0.25 resistance=220 package=THT]
  R42 = Resistor [tolerance=±5% power=0.25 resistance=220 package=THT]
  R43 = Resistor [tolerance=±5% power=0.25 resistance=220 package=THT]
  R44 = Resistor [tolerance=±5% power=0.25 resistance=220 package=THT]
  R45 = Resistor [tolerance=±5% power=0.25 resistance=220 package=THT]
  R46 = Resistor [tolerance=±5% power=0.25 resistance=220 package=THT]
  R47 = Resistor [tolerance=±5% power=0.25 resistance=220 package=THT]
  R48 = Resistor [tolerance=±5% power=0.25 resistance=220 package=THT]
  R49 = Resistor [tolerance=±5% power=0.25 resistance=220 package=THT]
  R50 = Resistor [tolerance=±5% power=0.25 resistance=220 package=THT]
  R51 = Resistor [tolerance=±5% power=0.25 resistance=220 package=THT]
  R52 = Resistor [tolerance=±5% power=0.25 resistance=220 package=THT]
  J26 = male pin header, 4 pins [form="♂ (male)"]
  U112 = TLP620-4 [package="DIP (Dual Inline) [THT]"]

nets:
  N1: U100.A0, J4.pin6, 2k2_Sil1.pin2
  N2: U100.A1, J4.pin5, 2k2_Sil1.pin3
  N3: U100.A2, J4.pin4, 2k2_Sil1.pin4
  N4: U100.P0, 2k2_Sil1.pin5, U104.pin16
  N5: U100.P1, 2k2_Sil1.pin6, U104.pin14
  N6: U100.P2, 2k2_Sil1.pin7, U104.pin12
  N7: U100.P3, 2k2_Sil1.pin8, U104.pin10
  GND: U100.GND, J4.pin1, J4.pin2, J4.pin3, U108.pin9, U108.pin11, U108.pin13, U108.pin15, U104.pin9, U104.pin11, U104.pin13, U104.pin15, J5.pin4, U105.pin9, U105.pin11, U105.pin13, U105.pin15, U101.GND, U109.pin9, U109.pin11, U109.pin13, U109.pin15, J9.pin1, J9.pin2, J9.pin3, U106.pin9, U106.pin11, U106.pin13, U106.pin15, U107.pin9, U107.pin11, U107.pin13, U107.pin15, U102.GND, U103.GND, J10.pin1, J10.pin2, J10.pin3, J11.pin1, J11.pin2, J11.pin3, U111.pin9, U111.pin11, U111.pin13, U111.pin15, J26.pin4, U112.pin9, U112.pin11, U112.pin13, U112.pin15
  N8: U100.P4, U108.pin16, 2k2_Sil5.pin2
  N9: U100.P5, U108.pin14, 2k2_Sil5.pin3
  N10: U100.P6, U108.pin12, 2k2_Sil5.pin4
  N11: U100.P7, U108.pin10, 2k2_Sil5.pin5
  I2C-SCL: U100.SCL, J5.pin3, U101.SCL, U102.SCL, U103.SCL, J26.pin3
  I2C-SDA: U100.SDA, J5.pin2, U101.SDA, U102.SDA, U103.SDA, J26.pin2
  3.3V: U100.VCC, 2k2_Sil1.pin1, J5.pin1, U101.VCC, 2k2_Sil3.pin1, 2k2_Sil4.pin1, 2k2_Sil5.pin1, U102.VCC, U103.VCC, 2k2_Sil6.pin1, 2k2_Sil7.pin1, 2k2_Sil8.pin1, 2k2_Sil9.pin1, J26.pin1
  N12: U108.pin1, R49.Pin_1
  N13: U108.pin2, U108.pin4, U108.pin6, U108.pin8, U109.pin2, U109.pin4, U109.pin6, U109.pin8, U111.pin2, U111.pin4, U111.pin6, U111.pin8, J18.pin1, J19.pin1, J20.pin1, J21.pin1, J22.pin1, J23.pin1, J24.pin1, J25.pin1, U112.pin2, U112.pin4, U112.pin6, U112.pin8
  N14: U108.pin3, R50.Pin_1
  N15: U108.pin5, R51.Pin_1
  N16: U108.pin7, R52.Pin_1
  N17: U104.pin1, R33.Pin_1
  N18: U104.pin2, U104.pin4, U104.pin6, U104.pin8, U105.pin2, U105.pin4, U105.pin6, U105.pin8, U106.pin2, U106.pin4, U106.pin6, U106.pin8, U107.pin2, U107.pin4, U107.pin6, U107.pin8, J8.pin1, J12.pin1, J13.pin1, J6.pin1, J7-4x470ohm.pin1, J14-4x470ohm.pin1, J15.pin1, J16.pin1
  N19: U104.pin3, R34.Pin_1
  N20: U104.pin5, R35.Pin_1
  N21: U104.pin7, R36.Pin_1
  N22: U105.pin1, R24.Pin_1
  N23: U105.pin3, R23.Pin_1
  N24: U105.pin5, R22.Pin_1
  N25: U105.pin7, R21.Pin_1
  N26: U105.pin10, U101.P3, 2k2_Sil3.pin8
  N27: U105.pin12, U101.P2, 2k2_Sil3.pin7
  N28: U105.pin14, U101.P1, 2k2_Sil3.pin6
  N29: U105.pin16, U101.P0, 2k2_Sil3.pin5
  N30: U101.A0, J9.pin6, 2k2_Sil3.pin2
  N31: U101.A1, J9.pin5, 2k2_Sil3.pin3
  N32: U101.A2, J9.pin4, 2k2_Sil3.pin4
  N33: U101.P4, U109.pin16, 2k2_Sil4.pin2
  N34: U101.P5, U109.pin14, 2k2_Sil4.pin3
  N35: U101.P6, U109.pin12, 2k2_Sil4.pin4
  N36: U101.P7, U109.pin10, 2k2_Sil4.pin5
  N37: U109.pin1, R45.Pin_1
  N38: U109.pin3, R46.Pin_1
  N39: U109.pin5, R47.Pin_1
  N40: U109.pin7, R48.Pin_1
  N41: U106.pin1, R25.Pin_1
  N42: U106.pin3, R26.Pin_1
  N43: U106.pin5, R27.Pin_1
  N44: U106.pin7, R28.Pin_1
  N45: U106.pin10, U102.P3, 2k2_Sil6.pin8
  N46: U106.pin12, U102.P2, 2k2_Sil6.pin7
  N47: U106.pin14, U102.P1, 2k2_Sil6.pin6
  N48: U106.pin16, U102.P0, 2k2_Sil6.pin5
  N49: U107.pin1, R29.Pin_1
  N50: U107.pin3, R30.Pin_1
  N51: U107.pin5, R31.Pin_1
  N52: U107.pin7, R32.Pin_1
  L107-10: U107.pin10, U103.P3, 2k2_Sil7.pin8
  L107-12: U107.pin12, U103.P2, 2k2_Sil7.pin7
  L107-14: U107.pin14, U103.P1, 2k2_Sil7.pin6
  L107-16: U107.pin16, U103.P0, 2k2_Sil7.pin5
  N53: U102.A0, 2k2_Sil6.pin2, J10.pin6
  N54: U102.A1, 2k2_Sil6.pin3, J10.pin5
  N55: U102.A2, 2k2_Sil6.pin4, J10.pin4
  N56: U102.P4, 2k2_Sil8.pin2, U111.pin16
  N57: U102.P5, 2k2_Sil8.pin3, U111.pin14
  N58: U102.P6, 2k2_Sil8.pin4, U111.pin12
  N59: U102.P7, 2k2_Sil8.pin5, U111.pin10
  N60: U103.A0, 2k2_Sil7.pin2, J11.pin6
  N61: U103.A1, 2k2_Sil7.pin3, J11.pin5
  N62: U103.A2, 2k2_Sil7.pin4, J11.pin4
  L17-16: U103.P4, 2k2_Sil9.pin2, U112.pin16
  L17-14: U103.P5, 2k2_Sil9.pin3, U112.pin14
  L17-12: U103.P6, 2k2_Sil9.pin4, U112.pin12
  L17-10: U103.P7, 2k2_Sil9.pin5, U112.pin10
  N63: U111.pin1, R41.Pin_1
  N64: U111.pin3, R42.Pin_1
  N65: U111.pin5, R43.Pin_1
  N66: U111.pin7, R44.Pin_1
  N67: J8.pin2, J16.pin2, R29.Pin_0
  N68: J8.pin3, J16.pin3, R30.Pin_0
  N69: J8.pin4, J16.pin4, R31.Pin_0
  N70: J8.pin5, J16.pin5, R32.Pin_0
  N71: J12.pin2, J15.pin2, R25.Pin_0
  N72: J12.pin3, J15.pin3, R26.Pin_0
  N73: J12.pin4, J15.pin4, R27.Pin_0
  N74: J12.pin5, J15.pin5, R28.Pin_0
  N75: J13.pin2, R24.Pin_0, J14-4x470ohm.pin2
  N76: J13.pin3, R23.Pin_0, J14-4x470ohm.pin3
  N77: J13.pin4, R22.Pin_0, J14-4x470ohm.pin4
  N78: J13.pin5, R21.Pin_0, J14-4x470ohm.pin5
  N79: J6.pin2, J7-4x470ohm.pin2, R33.Pin_0
  N80: J6.pin3, J7-4x470ohm.pin3, R34.Pin_0
  N81: J6.pin4, J7-4x470ohm.pin4, R35.Pin_0
  N82: J6.pin5, J7-4x470ohm.pin5, R36.Pin_0
  N83: J18.pin2, J22.pin2, R37.Pin_0
  N84: J18.pin3, J22.pin3, R38.Pin_0
  N85: J18.pin4, J22.pin4, R39.Pin_0
  N86: J18.pin5, J22.pin5, R40.Pin_0
  N87: J19.pin2, J23.pin2, R41.Pin_0
  N88: J19.pin3, J23.pin3, R42.Pin_0
  N89: J19.pin4, J23.pin4, R43.Pin_0
  N90: J19.pin5, J23.pin5, R44.Pin_0
  N91: J20.pin2, J24.pin2, R45.Pin_0
  N92: J20.pin3, J24.pin3, R46.Pin_0
  N93: J20.pin4, J24.pin4, R47.Pin_0
  N94: J20.pin5, J24.pin5, R48.Pin_0
  N95: J21.pin2, J25.pin2, R49.Pin_0
  N96: J21.pin3, J25.pin3, R50.Pin_0
  N97: J21.pin4, J25.pin4, R51.Pin_0
  N98: J21.pin5, J25.pin5, R52.Pin_0
  N99: R37.Pin_1, U112.pin1
  N100: R38.Pin_1, U112.pin3
  N101: R39.Pin_1, U112.pin5
  N102: R40.Pin_1, U112.pin7

notes:
  TrackSensor
  Svenn-Erik K. Thomsen
  sekt1953@gmail.com

custom parts:
  TLP620-4: Quad Photo-transistor optically coupled to two infrared emitting diodes connected in inverse parallel.
