# Fritzing sketch principle_track_detection (saved by Fritzing 0.9.6b)
breadboards: 1

parts:
  R1 = Resistor [tolerance=±5% power=0.25 resistance=22 package=THT]
  U1 = TLP620 [package="DIP (Dual Inline) [THT]"]
  Max = Resistor [tolerance=±5% power=0.25 resistance=2.2k package=THT]
  R2 = Resistor [tolerance=±5% power=0.25 resistance=2.2k package=THT]
  U2 = PCF8574 [package="DIP16 [THT]"]
  R3 = Resistor [tolerance=±5% power=0.25 resistance=470 package=THT]
  15VAC = Screw terminal - 2 pins [package=THT]
  J1 = male pin header, 1 pin [form="♂ (male)"]
  D1 = Rectifier Diode [part_number=1N4001 package="300 mil [THT]"]
  D2 = Rectifier Diode [part_number=1N4001 package="300 mil [THT]"]
  D3 = Rectifier Diode [part_number=1N4001 package="300 mil [THT]"]
  D4 = Rectifier Diode [part_number=1N4001 package="300 mil [THT]"]
  D5 = Rectifier Diode [part_number=1N4001 package="300 mil [THT]"]
  D6 = Rectifier Diode [part_number=1N4001 package="300 mil [THT]"]
  J2 = male pin header, 1 pin [form="♂ (male)"]
  Skinde_afsnit = Screw terminal - 2 pins [package=THT]

nets:
  N1: R1.Pin_0, U1.pin1
  N2: R1.Pin_1, Max.Pin_1, R3.Pin_0, J1.pin1, D1.cathode, D6.anode, Skinde_afsnit.pin1
  15V: U1.pin2, R3.Pin_1, 15VAC.pin1, D3.anode, D4.cathode, J2.pin1
  GND: U1.pin3, Max.Pin_0, U2.GND, 15VAC.pin2, Skinde_afsnit.pin2
  N3: U1.pin4, R2.Pin_1, U2.P1
  3.3V: R2.Pin_0, U2.VCC
  N4: D1.anode, D2.cathode
  N5: D2.anode, D3.cathode
  N6: D4.anode, D5.cathode
  N7: D5.anode, D6.cathode

custom parts:
  TLP620: Photo-transistor optically coupled to two infrared emitting diodes connected in inverse parallel.
